# Fritzing sketch rgb (saved by Fritzing 0.8.5b)
breadboards: 1

parts:
  R1 = Resistor [tolerance=±5% resistance=220 package=THT]
  LED3 = RGB LED (com. cathode, rgb) [package="5 mm [THT]"]
  R2 = Resistor [tolerance=±5% resistance=220 package=THT]
  R3 = Resistor [tolerance=±5% resistance=220 package=THT]
  Parte1 = Arduino Uno (Rev3)
  LED4 = LED - 5mm [color="White (6500K)" package="5 mm [THT]"]
  R4 = Resistor [tolerance=±5% resistance=220 package=THT]
  BAT1 = BC9VPC [package=bc9vpc]

nets:
  N1: R1.Pin_0, Parte1.D11_PWM/MOSI
  N2: R1.Pin_1, LED3.red_anode
  N3: LED3.common_cathode, Parte1.GND, LED4.cathode, BAT1.V+
  N4: LED3.green_anode, R2.Pin_1
  N5: LED3.blue_anode, R3.Pin_1
  N6: R2.Pin_0, Parte1.D10_PWM/SS
  N7: R3.Pin_0, Parte1.D9_PWM
  N8: Parte1.D2, R4.Pin_0
  N9: Parte1.VIN, BAT1.V-
  N10: LED4.anode, R4.Pin_1
